# Fritzing sketch Untitled Sketch 2 (saved by Fritzing 0.9.3b)
circuit board: 8.46667cm x 5.64444cm
breadboards: 1

parts:
  OMRON1 = OMRON PCB Power Relay – G5LE [part_number="G5LE-1\n" package=THT]
  LED1 = LED - 5mm [color="Red (633nm)" package="5 mm [THT]"]
  R1 = Resistor [tolerance=±5% resistance=1k package=THT]
  Q1 = TRANSISTOR_NPN [package=to-92-ammo]
  R2 = Resistor [tolerance=±5% resistance=1k package=THT]
  R3 = Resistor [tolerance=±5% resistance=1k package=THT]
  LED2 = LED - 5mm [color="Red (633nm)" package="5 mm [THT]"]
  D1 = Diode [package=diode-1n4001]
  L1 = Inductor [package="400 mil [THT]"]
  7_Segment1 = 7 Segment Display

nets:
  N1: OMRON1.COIL1, Q1.C, LED2.cathode, D1.A
  5V: OMRON1.COIL2, R1.Pin_0, R3.Pin_0, D1.C, L1.pin_0
  GND: LED1.cathode, Q1.E, 7_Segment1.common_anode
  N2: LED1.anode, R1.Pin_1
  N3: Q1.B, R2.Pin_1
  Inpute: R2.Pin_0
  N4: R3.Pin_1, LED2.anode
