# Fritzing sketch V2.PCB mamie_Blue (saved by Fritzing 0.9.3b)
circuit board: 15cm x 9cm
breadboards: 1

parts:
  Arduino_nano = Arduino Uno (Rev3)
  HC06 = Bluetooth HC-06u [package=THT]
  2K = Resistor [tolerance=±5% resistance=2k package=THT]
  1K = Resistor [tolerance=±5% resistance=1k package=THT]
  100K = Resistor [tolerance=±5% resistance=100k package=THT]
  100K_2 = Resistor [tolerance=±5% resistance=100k package=THT]
  0_Rupteur = OMRON PCB Power Relay – G5LE [part_number="G5LE-1\n" package=THT]
  4_Extrat_2 = OMRON PCB Power Relay – G5LE [part_number="G5LE-1\n" package=THT]
  2_Extra_1 = OMRON PCB Power Relay – G5LE [part_number="G5LE-1\n" package=THT]
  1_Ventil_moteur = OMRON PCB Power Relay – G5LE [part_number="G5LE-1\n" package=THT]
  C1 = Electrolytic Capacitor [capacitance=1µF package="100 mil [THT, electrolytic]"]
  C2 = Electrolytic Capacitor [capacitance=1µF package="100 mil [THT, electrolytic]"]
  DHT11-OUT = PNP-Transistor [package="TO92 [THT]"]
  100K_3 = Resistor [tolerance=±5% resistance=100k package=THT]
  100K_4 = Resistor [tolerance=±5% resistance=100k package=THT]
  C4 = Electrolytic Capacitor [capacitance=1µF package="100 mil [THT, electrolytic]"]
  C5 = Electrolytic Capacitor [capacitance=1µF package="100 mil [THT, electrolytic]"]
  DHT11-IN = PNP-Transistor [package="TO92 [THT]"]

nets:
  N1: Arduino_nano.A0, 100K.Pin_1, C2.+
  N2: Arduino_nano.A1, 100K_2.Pin_1, C1.+
  N3: Arduino_nano.A2, 100K_4.Pin_1, C4.-
  N4: Arduino_nano.A3, 100K_3.Pin_1, C5.-
  N5: Arduino_nano.D8, DHT11-OUT.E
  N6: Arduino_nano.D9_PWM, DHT11-IN.E
  GND: Arduino_nano.GND, HC06.GND, 2K.Pin_0, 100K.Pin_0, 100K_2.Pin_0, 0_Rupteur.COIL2, 4_Extrat_2.COIL2, 2_Extra_1.COIL2, 1_Ventil_moteur.COIL2, DHT11-OUT.C, 100K_3.Pin_0, 100K_4.Pin_0, DHT11-IN.C
  N7: Arduino_nano.D2, HC06.TXD
  N8: Arduino_nano.D3_PWM, 1K.Pin_1
  N9: Arduino_nano.D4, 1_Ventil_moteur.C
  N10: Arduino_nano.D5_PWM, 2_Extra_1.C
  N11: Arduino_nano.D6_PWM, 4_Extrat_2.C
  N12: Arduino_nano.D7, 0_Rupteur.C
  5V: Arduino_nano.5V, HC06.VCC, 0_Rupteur.COIL1, 4_Extrat_2.COIL1, 2_Extra_1.COIL1, 1_Ventil_moteur.COIL1, C1.-, C2.-, DHT11-OUT.B, C4.+, C5.+, DHT11-IN.B
  N13: HC06.RXD, 2K.Pin_1, 1K.Pin_0

custom parts:
  Bluetooth HC-06u: Bluetooth HC-06 - face up, pins down 16.5mm x 37.5mm PCB
