# Fritzing sketch V3.PCB mamie_Blue (saved by Fritzing 0.9.3b)
circuit board: 15cm x 9cm
breadboards: 1

parts:
  Arduino_nano = Arduino Uno (Rev3)
  HC06 = Bluetooth HC-06u [package=THT]
  2K = Resistor [tolerance=±5% resistance=2k package=THT]
  1K = Resistor [tolerance=±5% resistance=1k package=THT]
  100K = Resistor [tolerance=±5% resistance=100k package=THT]
  100K_2 = Resistor [tolerance=±5% resistance=100k package=THT]
  C1 = Electrolytic Capacitor [capacitance=1µF package="100 mil [THT, electrolytic]"]
  C2 = Electrolytic Capacitor [capacitance=1µF package="100 mil [THT, electrolytic]"]
  DHT11-OUT = PNP-Transistor [package="TO92 [THT]"]
  100K_3 = Resistor [tolerance=±5% resistance=100k package=THT]
  100K_4 = Resistor [tolerance=±5% resistance=100k package=THT]
  C4 = Electrolytic Capacitor [capacitance=1µF package="100 mil [THT, electrolytic]"]
  C5 = Electrolytic Capacitor [capacitance=1µF package="100 mil [THT, electrolytic]"]
  DHT11-IN = PNP-Transistor [package="TO92 [THT]"]
  OMRON4 = OMRON PCB Power Relay – G5LE [part_number="G5LE-1\n" package=THT]
  LED = LED - 5mm [color="Red (633nm)" package="5 mm [THT]"]
  LED_2 = LED - 5mm [color="Green (555nm)" package="5 mm [THT]"]
  1K_2 = Resistor [tolerance=±5% resistance=1k package=THT]
  1K_3 = Resistor [tolerance=±5% resistance=1k package=THT]
  1k = Resistor [tolerance=±5% resistance=1k package=THT]
  NPN = TRANSISTOR_NPN [package=to-92-ammo]
  Diode = Diode [package=diode-1n4001]

nets:
  N1: Arduino_nano.A0, 100K.Pin_1, C2.+
  N2: Arduino_nano.A1, 100K_2.Pin_1, C1.+
  N3: Arduino_nano.A2, 100K_4.Pin_1, C4.-
  N4: Arduino_nano.A3, 100K_3.Pin_1, C5.-
  N5: Arduino_nano.D8, DHT11-OUT.E
  N6: Arduino_nano.D9_PWM, DHT11-IN.E
  GND: Arduino_nano.GND, HC06.GND, 2K.Pin_0, 100K.Pin_0, 100K_2.Pin_0, DHT11-OUT.C, 100K_3.Pin_0, 100K_4.Pin_0, DHT11-IN.C, LED.cathode, NPN.E
  N7: Arduino_nano.D2, HC06.TXD
  N8: Arduino_nano.D3_PWM, 1K.Pin_1
  Inpute: Arduino_nano.D7, 1K_3.Pin_0
  5V: Arduino_nano.5V, HC06.VCC, C1.-, C2.-, DHT11-OUT.B, C4.+, C5.+, DHT11-IN.B, OMRON4.COIL2, 1K_2.Pin_0, 1k.Pin_0, Diode.C
  N9: HC06.RXD, 2K.Pin_1, 1K.Pin_0
  N10: OMRON4.COIL1, LED_2.cathode, NPN.C, Diode.A
  N11: LED.anode, 1k.Pin_1
  N12: LED_2.anode, 1K_2.Pin_1
  N13: 1K_3.Pin_1, NPN.B

custom parts:
  Bluetooth HC-06u: Bluetooth HC-06 - face up, pins down 16.5mm x 37.5mm PCB
