# Fritzing sketch V6.PCB mamie_Blue (saved by Fritzing 0.9.3b)
breadboards: 1

parts:
  Arduino_nano = Arduino Nano (Rev3.0)
  HC06 = Bluetooth HC-06u [package=THT]
  R18 = Resistor [tolerance=±5% resistance=2k package=THT]
  R17 = Resistor [tolerance=±5% resistance=1k package=THT]
  RE1 = OMRON PCB Power Relay – G5LE [part_number="G5LE-1\n" package=THT]
  R15 = Resistor [tolerance=±5% resistance=1k package=THT]
  R16 = Resistor [tolerance=±5% resistance=1k package=THT]
  R14 = Resistor [tolerance=±5% resistance=1k package=THT]
  D3 = Diode [package=diode-1n4001]
  IC1 = Voltage Regulator [package=78xxl]
  J1 = screw terminal, 2 pins
  RE2 = OMRON PCB Power Relay – G5LE [part_number="G5LE-1\n" package=THT]
  R12 = Resistor [tolerance=±5% resistance=1k package=THT]
  R13 = Resistor [tolerance=±5% resistance=1k package=THT]
  R11 = Resistor [tolerance=±5% resistance=1k package=THT]
  NPN2 = TRANSISTOR_NPN [package=to-92-ammo]
  D4 = Diode [package=diode-1n4001]
  J3 = screw terminal, 3 pins
  RE3 = OMRON PCB Power Relay – G5LE [part_number="G5LE-1\n" package=THT]
  R9 = Resistor [tolerance=±5% resistance=1k package=THT]
  R10 = Resistor [tolerance=±5% resistance=1k package=THT]
  R8 = Resistor [tolerance=±5% resistance=1k package=THT]
  NPN3 = TRANSISTOR_NPN [package=to-92-ammo]
  D5 = Diode [package=diode-1n4001]
  J4 = screw terminal, 3 pins
  LED5 = LED - 3mm [color="Red (633nm)" package="3 mm [THT]"]
  LED6 = LED - 3mm [color="Green (555nm)" package="3 mm [THT]"]
  LED3 = LED - 3mm [color="Red (633nm)" package="3 mm [THT]"]
  LED4 = LED - 3mm [color="Green (555nm)" package="3 mm [THT]"]
  LED2 = LED - 3mm [color="Red (633nm)" package="3 mm [THT]"]
  LED1 = LED - 3mm [color="Green (555nm)" package="3 mm [THT]"]
  RE4 = OMRON PCB Power Relay – G5LE [part_number="G5LE-1\n" package=THT]
  LED8 = LED - 3mm [color="Green (555nm)" package="3 mm [THT]"]
  LED7 = LED - 3mm [color="Red (633nm)" package="3 mm [THT]"]
  R6 = Resistor [tolerance=±5% resistance=1k package=THT]
  R7 = Resistor [tolerance=±5% resistance=1k package=THT]
  R5 = Resistor [tolerance=±5% resistance=1k package=THT]
  NPN4 = TRANSISTOR_NPN [package=to-92-ammo]
  D6 = Diode [package=diode-1n4001]
  J5 = screw terminal, 3 pins
  C1 = Electrolytic Capacitor [capacitance=100µF package="100 mil [THT, electrolytic]"]
  C2 = Electrolytic Capacitor [capacitance=10µF package="100 mil [THT, electrolytic]"]
  D2 = Diode [package=diode-1n4001]
  D1 = Diode [package=diode-1n4001]
  R1 = Resistor [tolerance=±5% resistance=100k package=THT]
  R3 = Resistor [tolerance=±5% resistance=100k package=THT]
  R4 = Resistor [tolerance=±5% resistance=100k package=THT]
  R2 = Resistor [tolerance=±5% resistance=100k package=THT]
  S4 = Tilt Switch [package=THT]
  S3 = Tilt Switch [package=THT]
  S1 = Tilt Switch [package=THT]
  S2 = Tilt Switch [package=THT]
  RF443 = AD22100 - Voltage Output Temperature Sensor with Signal Conditioning [part_number=AD22100]
  I2C = Ceramic Capacitor [capacitance=100nF voltage=16V package="100 mil [THT, multilayer]"]
  IC2 = Voltage Regulator [package=78xxl]
  C3 = Electrolytic Capacitor [capacitance=0.1µF package="100 mil [THT, electrolytic]"]
  C4 = Electrolytic Capacitor [capacitance=1µF package="100 mil [THT, electrolytic]"]
  BP5V = Tilt Switch [package=THT]
  DHT11_IN = AD22100 - Voltage Output Temperature Sensor with Signal Conditioning [part_number=AD22100]
  DHT11_OUT = AD22100 - Voltage Output Temperature Sensor with Signal Conditioning [part_number=AD22100]
  NPN1 = TRANSISTOR_NPN [package=to-92-ammo]
  J2 = screw terminal, 3 pins

nets:
  GND: Arduino_nano.GND, HC06.GND, R18.Pin_0, IC1.GND, NPN2.E, NPN3.E, LED5.cathode, LED3.cathode, LED2.cathode, LED7.cathode, NPN4.E, C1.-, C2.-, D2.C, R1.Pin_1, R3.Pin_1, R4.Pin_1, R2.Pin_1, RF443.GND, IC2.GND, C3.-, C4.-, DHT11_IN.GND, DHT11_OUT.GND, NPN1.E
  N1: Arduino_nano.D2, HC06.TXD
  N2: Arduino_nano.D3, R17.Pin_1
  N3: Arduino_nano.D4, R7.Pin_0
  N4: Arduino_nano.D5, R10.Pin_0
  N5: Arduino_nano.D6, R13.Pin_0
  N6: Arduino_nano.D7, R16.Pin_0
  N7: Arduino_nano.D8, DHT11_IN.Vo
  N8: Arduino_nano.D9, DHT11_OUT.Vo
  N9: Arduino_nano.D10, RF443.Vo
  N10: Arduino_nano.VIN, IC2.OUT, C4.+
  5V: Arduino_nano.5V, HC06.VCC, BP5V.Pin_2
  N11: Arduino_nano.A5, I2C.0
  N12: Arduino_nano.A4, I2C.1
  N13: Arduino_nano.A3, R2.Pin_0, S2.Pin_2
  N14: Arduino_nano.A2, R1.Pin_0, S1.Pin_2
  N15: Arduino_nano.A1, R3.Pin_0, S3.Pin_2
  N16: Arduino_nano.A0, R4.Pin_0, S4.Pin_2
  N17: HC06.RXD, R18.Pin_1, R17.Pin_0
  N18: RE1.A, J2.pin3
  N19: RE1.COIL1, D3.A, LED1.cathode, NPN1.C
  N20: RE1.C, J2.pin2
  N21: RE1.COIL2, R15.Pin_0, R14.Pin_0, D3.C, IC1.OUT, RE2.COIL2, R12.Pin_0, R11.Pin_0, D4.C, RE3.COIL2, R9.Pin_0, R8.Pin_0, D5.C, RE4.COIL2, R6.Pin_0, R5.Pin_0, D6.C, C2.+, S4.Pin_1, S3.Pin_1, S1.Pin_1, S2.Pin_1, RF443.V+, BP5V.Pin_1, DHT11_IN.V+, DHT11_OUT.V+
  N22: RE1.B, J2.pin1
  N23: R15.Pin_1, LED2.anode
  N24: R16.Pin_1, NPN1.B
  N25: R14.Pin_1, LED1.anode
  N26: IC1.IN, C1.+, D1.A, IC2.IN, C3.+
  N27: J1.pin1, D2.A
  N28: J1.pin2, D1.C
  N29: RE2.A, J3.pin3
  N30: RE2.COIL1, NPN2.C, D4.A, LED4.cathode
  N31: RE2.C, J3.pin2
  N32: RE2.B, J3.pin1
  N33: R12.Pin_1, LED3.anode
  N34: R13.Pin_1, NPN2.B
  N35: R11.Pin_1, LED4.anode
  N36: RE3.A, J4.pin3
  N37: RE3.COIL1, NPN3.C, D5.A, LED6.cathode
  N38: RE3.C, J4.pin2
  N39: RE3.B, J4.pin1
  N40: R9.Pin_1, LED5.anode
  N41: R10.Pin_1, NPN3.B
  N42: R8.Pin_1, LED6.anode
  N43: RE4.A, J5.pin3
  N44: RE4.COIL1, LED8.cathode, NPN4.C, D6.A
  N45: RE4.C, J5.pin2
  N46: RE4.B, J5.pin1
  N47: LED8.anode, R5.Pin_1
  N48: LED7.anode, R6.Pin_1
  N49: R7.Pin_1, NPN4.B

notes:
  +12-14V
  Mustang ECU
  VCC
  GND
  5V
  9V

custom parts:
  Bluetooth HC-06u: Bluetooth HC-06 - face up, pins down 16.5mm x 37.5mm PCB
